# Fritzing sketch doorbellNotifier (saved by Fritzing 0.9.3b)
breadboards: 1

parts:
  Onderdeel1 = Arduino Nano (Rev3.0)
  R1 = Resistor [tolerance=±5% resistance=15k package=THT]
  R2 = Resistor [tolerance=±5% resistance=10k package=THT]
  J1 = screw terminal, 2 pins
  J2 = screw terminal, 2 pins

nets:
  N1: Onderdeel1.GND, R2.Pin_0, J2.pin1
  N2: Onderdeel1.D2, R1.Pin_0, R2.Pin_1
  N3: Onderdeel1.VIN, J1.pin2, J2.pin2
  N4: R1.Pin_1, J1.pin1

notes:
  12v in
  switch
